# Fritzing sketch 07_3LED (saved by Fritzing 0.9.4)
breadboards: 1

parts:
  Mod1 = Raspberry Pi Pico
  LED4 = smd LED [color="Red (633nm)" package="0805 [SMD]"]
  LED5 = smd LED [color="Yellow (585nm)" package="0805 [SMD]"]
  LED6 = smd LED [color="Green (555nm)" package="0805 [SMD]"]
  R1 = Resistor [tolerance=±5% resistance=220 package="0805 [SMD]"]
  LED7 = smd LED [color="Red (633nm)" package="0805 [SMD]"]
  LED8 = smd LED [color="Yellow (592nm)" package="0805 [SMD]"]
  LED9 = smd LED [color="Green (555nm)" package="0805 [SMD]"]

nets:
  N1: Mod1.pin_3, Mod1.pin_8, Mod1.pin_13, Mod1.pin_18, Mod1.pin_23, Mod1.pin_28, Mod1.pin_33, Mod1.pin_38, R1.Pin_1
  N2: Mod1.pin_17, LED4.anode
  N3: Mod1.pin_19, LED6.anode
  N4: Mod1.pin_20, LED5.anode
  N5: Mod1.pin_21, LED8.anode
  N6: Mod1.pin_22, LED9.anode
  N7: Mod1.pin_24, LED7.anode
  N8: LED4.cathode, LED5.cathode, LED6.cathode, R1.Pin_0, LED7.cathode, LED8.cathode, LED9.cathode

custom parts:
  Raspberry Pi Pico: Raspberry Pi Pico. Based around the RP2040 microcontroller the Pico is a low cost microcontroller device bringing Raspberry Pi quality, cost, and easy of use to the microcontroller space. Jan 2021, Split part in to two versions: tht (this one) and SMD. This one will drill holes for a .1 in header in pcb to allow plugging in the module as well as providing pads to solder the module to the top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
