# Fritzing sketch 04_LED_6_button (saved by Fritzing 0.9.4)
breadboards: 1

parts:
  Mod1 = Raspberry Pi Pico  # not connected
  R1 = Resistor [tolerance=±5% resistance=220 package=THT]
  LED3 = smd LED [color="Green (555nm)" package="0805 [SMD]"]
  LED2 = smd LED [color="Yellow (585nm)" package="0805 [SMD]"]
  LED1 = smd LED [color="Red (633nm)" package="0805 [SMD]"]
  S2 = Pushbutton [package="[SMD]"]
  S3 = Pushbutton [package="[SMD]"]

nets:
  N1: R1.Pin_0, LED3.cathode, LED2.cathode, LED1.cathode
  N2: R1.Pin_1, S2.Pin_1, S2.Pin_2, S3.Pin_1, S3.Pin_2
  N3: S2.Pin_3, S2.Pin_4
  N4: S3.Pin_3, S3.Pin_4

custom parts:
  Raspberry Pi Pico: Raspberry Pi Pico. Based around the RP2040 microcontroller the Pico is a low cost microcontroller device bringing Raspberry Pi quality, cost, and easy of use to the microcontroller space. Jan 2021, Split part in to two versions: tht (this one) and SMD. This one will drill holes for a .1 in header in pcb to allow plugging in the module as well as providing pads to solder the module to the top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
